# Fritzing sketch ESP8266 Base (saved by Fritzing 0.9.2b)
breadboards: 1

parts:
  U1 = ESP8266 WiFi Module [part_number=ESP8266]
  S1 = Pushbutton [package="[THT]"]
  LED1 = LED - 5mm [color="Red (633nm)" package="5 mm [THT]"]
  S2 = Pushbutton [package="[THT]"]
  Part1 = FTDI Basic Programmer
  Part2 = Arduino Uno (Rev3) - ICSP

nets:
  N1: U1.RXD, Part1.TXO
  VCC: U1.VCC, U1.CH_PD, LED1.cathode, Part2.3V3
  GND: U1.GPIO_2, U1.GND, U1.GPIO_15, U1.REST, S1.Pin_1, S1.Pin_2, S1.Pin_3, S1.Pin_4, S2.Pin_1, S2.Pin_2, S2.Pin_3, S2.Pin_4, Part1.GND, Part2.GND
  N2: U1.TXD, Part1.RXI
  N3: U1.GPIO_14, LED1.anode

notes:
  Reset
  Program
